# Fritzing sketch schematic_arduino_IR-NEW (saved by Fritzing 0.9.3b)
breadboards: 1

parts:
  IR1 = TSOP312.., 314.. [package=THT]
  J1 = Basic Servo
  R3 = Resistor [tolerance=±5% resistance=10k package=THT]
  R2 = Resistor [tolerance=±5% resistance=10k package=THT]
  R4 = Resistor [tolerance=±5% resistance=10k package=THT]
  R5 = Resistor [tolerance=±5% resistance=10k package=THT]
  R6 = Resistor [tolerance=±5% resistance=1 package=THT]
  C1 = Ceramic Capacitor [capacitance=10nF package="100 mil [THT, multilayer]"]
  C2 = Ceramic Capacitor [capacitance=10nF package="100 mil [THT, multilayer]"]
  S1 = SWITCH-MOMENTARY-2 [package=tactile-pth-12mm]
  R11 = Resistor [tolerance=±5% resistance=1 package=THT]
  R10 = 1k Ω Resistor [package=THT]
  Blue_RIGHT = green smd LED [package="1206 [SMD]"]
  R1 = 10k Ω Resistor [package=THT]
  Encoder_LED = green smd LED [package="1206 [SMD]"]
  R8 = 1k Ω Resistor [package=THT]
  R9 = 1k Ω Resistor [package=THT]
  Yellow = green smd LED [package="1206 [SMD]"]
  RE1 = Rotary Encoder [package=THT]
  R7 = 1k Ω Resistor [package=THT]
  Arduino1 = Arduino
  Blue_LEFT = green smd LED [package="1206 [SMD]"]
  Gree = green smd LED [package="1206 [SMD]"]

nets:
  N1: IR1.GND, R11.Pin_1
  5V: IR1.Vs, J1.vcc, R4.Pin_0, R5.Pin_1, R1.Pin_0, RE1.EncoderPinB, Arduino1.+5V
  N2: IR1.Data, Arduino1.D6
  GND: J1.gnd, R2.Pin_0, C1.0, C2.1, S1.1, R11.Pin_0, Blue_RIGHT.cathode, Encoder_LED.cathode, Yellow.cathode, Arduino1.GND, Arduino1.D12, Blue_LEFT.cathode, Gree.cathode
  N3: J1.pulse, Arduino1.D9
  N4: R3.Pin_0, C1.1, Arduino1.D11
  N5: R3.Pin_1, R4.Pin_1, RE1.EncoderPinA
  N6: R2.Pin_1, R5.Pin_0, RE1.EncoderPinC
  N7: R6.Pin_0, Arduino1.D10
  N8: R6.Pin_1, Encoder_LED.anode
  N9: S1.2, R1.Pin_1, Arduino1.D8
  N10: R10.Pin_0, Blue_LEFT.anode
  N11: R10.Pin_1, Arduino1.D7
  N12: Blue_RIGHT.anode, R9.Pin_0
  N13: R8.Pin_0, Yellow.anode
  N14: R8.Pin_1, Arduino1.D4
  N15: R9.Pin_1, Arduino1.D5
  N16: R7.Pin_0, Gree.anode
  N17: R7.Pin_1, Arduino1.D3
