# Fritzing sketch schematic_arduino_IR-2 (saved by Fritzing 0.7.10b)
breadboards: 1

parts:
  Arduino1 = Arduino
  IR1 = TSOP312.., 314.. [package=THT]
  R1 = 10k Ω Resistor [package=THT]
  J1 = Basic Servo
  RE1 = Rotary Encoder [package=THT]
  R2 = 10k Ω Resistor [package=THT]
  R3 = 10k Ω Resistor [package=THT]
  Gree = green smd LED [package="1206 [SMD]"]
  R4 = 10k Ω Resistor [package=THT]
  Yellow = green smd LED [package="1206 [SMD]"]
  R5 = 10k Ω Resistor [package=THT]
  Blue_RIGHT = green smd LED [package="1206 [SMD]"]
  R6 = 10k Ω Resistor [package=THT]
  Blue_LEFT = green smd LED [package="1206 [SMD]"]
  R7 = 10k Ω Resistor [package=THT]
  Encoder_LED = green smd LED [package="1206 [SMD]"]
  R8 = 10k Ω Resistor [package=THT]
  Push_Button = Pushbutton [package="[THT]"]
  R9 = 10k Ω Resistor [package=THT]

nets:
  GND: Arduino1.GND, J1.gnd, Gree.cathode, Yellow.cathode, Blue_RIGHT.cathode, Blue_LEFT.cathode, Encoder_LED.cathode, Push_Button.Pin_1, Push_Button.Pin_2
  N1: Arduino1.D12, RE1.EncoderPinA, R2.Pin_1
  N2: Arduino1.D11, RE1.EncoderPinB, R3.Pin_1
  N3: Arduino1.D10, R8.Pin_1
  N4: Arduino1.D9, J1.pulse
  N5: Arduino1.D8, Push_Button.Pin_3, R9.Pin_0
  N6: Arduino1.D7, R7.Pin_0
  N7: Arduino1.D6, IR1.Data
  N8: Arduino1.D5, R6.Pin_0
  N9: Arduino1.D4, R5.Pin_0
  N10: Arduino1.D3, R4.Pin_0
  N11: Arduino1.+5V, R2.Pin_0
  N12: IR1.GND, R1.Pin_0
  5V: IR1.Vs, J1.vcc, R9.Pin_1
  N13: Encoder_LED.anode, R8.Pin_0

notes:
  R1, R2, R3 = 10K
